// Logisim project common bus final.circ as structural Verilog
module main (
  input  in_1,
  input  [2:0] in_2,
  input  [1:0] in_3,
  input  in_4,
  input  [2:0] SOURCE_SELECTION,
  input  [3:0] in_6,
  input  [3:0] in_7,
  input  [3:0] in_8,
  input  [3:0] in_9,
  input  [3:0] in_10,
  input  [2:0] in_11,
  output NO_REGISTER,
  output [3:0] out_13,
  output [3:0] out_14
);

  wire clock_1_out, decoder_1_out0, decoder_1_out1, decoder_1_out2, decoder_1_out3, decoder_1_out4,
       decoder_1_out5, decoder_1_out6, undriven;
  wire [3:0] bus_system_1_out_10, multiplexer_1_out, multiplexer_2_out, multiplexer_4_out, multiplexer_6_out,
       multiplexer_7_out, multiplexer_9_out, multiplexer_11_out, register_1_q, register_2_q, register_3_q,
       register_4_q, register_5_q, register_6_q, register_7_q;

  bus_system bus_system_1 (
    .in_2(in_3), .in_3(in_9), .in_4(in_10), .in_5(in_7), .in_6(in_8), .out_7(bus_system_1_out_10[3]),
    .out_8(bus_system_1_out_10[2]), .out_9(bus_system_1_out_10[1]), .out_10(bus_system_1_out_10[0]),
    .in_1(in_4));
  Multiplexer #(.width(4)) multiplexer_1 (
    .in0(register_1_q), .in1(out_14), .out(multiplexer_1_out), .sel(decoder_1_out0));  // open: en
  Register #(.width(4)) register_1 (.D(multiplexer_1_out), .Q(register_1_q), .clk(clock_1_out));  // open: en, clr
  Clock clock_1 (.out(clock_1_out));
  Multiplexer #(.width(4)) multiplexer_2 (
    .in0(register_2_q), .in1(out_14), .out(multiplexer_2_out), .sel(decoder_1_out1));  // open: en
  Register #(.width(4)) register_2 (.D(multiplexer_2_out), .Q(register_2_q), .clk(clock_1_out));  // open: en, clr
  Multiplexer #(.select(3)) multiplexer_3 (
    .in0(register_1_q[0]), .in1(register_2_q[0]), .in2(register_3_q[0]), .in3(register_4_q[0]),
    .in4(register_5_q[0]), .in5(register_6_q[0]), .in6(register_7_q[0]), .in7(bus_system_1_out_10[0]),
    .out(out_14[0]), .sel(SOURCE_SELECTION));  // open: en
  Multiplexer #(.width(4)) multiplexer_4 (
    .in0(register_3_q), .in1(out_14), .out(multiplexer_4_out), .sel(decoder_1_out2));  // open: en
  Register #(.width(4)) register_3 (.D(multiplexer_4_out), .Q(register_3_q), .clk(clock_1_out));  // open: en, clr
  Multiplexer #(.select(3)) multiplexer_5 (
    .in0(register_1_q[1]), .in1(register_2_q[1]), .in2(register_3_q[1]), .in3(register_4_q[1]),
    .in4(register_5_q[1]), .in5(register_6_q[1]), .in6(register_7_q[1]), .in7(bus_system_1_out_10[1]),
    .out(out_14[1]), .sel(SOURCE_SELECTION));  // open: en
  Multiplexer #(.width(4)) multiplexer_6 (
    .in0(register_4_q), .in1(out_14), .out(multiplexer_6_out), .sel(decoder_1_out3));  // open: en
  Register #(.width(4)) register_4 (.D(multiplexer_6_out), .Q(register_4_q), .clk(clock_1_out));  // open: en, clr
  Multiplexer #(.width(4)) multiplexer_7 (
    .in0(register_5_q), .in1(out_14), .out(multiplexer_7_out), .sel(decoder_1_out4));  // open: en
  Register #(.width(4)) register_5 (.D(multiplexer_7_out), .Q(register_5_q), .clk(clock_1_out));  // open: en, clr
  Multiplexer #(.select(3)) multiplexer_8 (
    .in0(register_1_q[2]), .in1(register_2_q[2]), .in2(register_3_q[2]), .in3(register_4_q[2]),
    .in4(register_5_q[2]), .in5(register_6_q[2]), .in6(register_7_q[2]), .in7(bus_system_1_out_10[2]),
    .out(out_14[2]), .sel(SOURCE_SELECTION));  // open: en
  Multiplexer #(.width(4)) multiplexer_9 (
    .in0(register_6_q), .in1(out_14), .out(multiplexer_9_out), .sel(decoder_1_out5));  // open: en
  Register #(.width(4)) register_6 (.D(multiplexer_9_out), .Q(register_6_q), .clk(clock_1_out));  // open: en, clr
  Multiplexer #(.select(3)) multiplexer_10 (
    .in0(register_1_q[3]), .in1(register_2_q[3]), .in2(register_3_q[3]), .in3(register_4_q[3]),
    .in4(register_5_q[3]), .in5(register_6_q[3]), .in6(register_7_q[3]), .in7(bus_system_1_out_10[3]),
    .out(out_14[3]), .sel(SOURCE_SELECTION));  // open: en
  Multiplexer #(.width(4)) multiplexer_11 (
    .in0(register_7_q), .in1(out_14), .out(multiplexer_11_out), .sel(decoder_1_out6));  // open: en
  Register #(.width(4)) register_7 (.D(multiplexer_11_out), .Q(register_7_q), .clk(clock_1_out));  // open: en, clr
  BASIC_ALU basic_alu_1 (.A(out_14), .B(in_6), .in_3(in_11), .out_4(out_13));
  Decoder #(.select(3)) decoder_1 (
    .out0(decoder_1_out0), .out1(decoder_1_out1), .out2(decoder_1_out2), .out3(decoder_1_out3),
    .out4(decoder_1_out4), .out5(decoder_1_out5), .out6(decoder_1_out6), .out7(NO_REGISTER), .sel(in_2),
    .en(undriven));

  // Notes on the sheet:
  //   COMMON BUS SYSTEM
  //   2k19/IT/142 VIKAS BHANDARI
  //   2K19/IT/136 UTKARSH 
  //   DEBUG
  //   DESTINATION SELECTION
endmodule

module bus_system (
  input  in_1,
  input  [1:0] in_2,
  input  [3:0] in_3,
  input  [3:0] in_4,
  input  [3:0] in_5,
  input  [3:0] in_6,
  output out_7,
  output out_8,
  output out_9,
  output out_10
);

  Multiplexer #(.select(2)) multiplexer_1 (
    .in0(in_5[3]), .in1(in_6[3]), .in2(in_3[3]), .in3(in_4[3]), .out(out_7), .sel(in_2), .en(in_1));
  Multiplexer #(.select(2)) multiplexer_2 (
    .in0(in_5[2]), .in1(in_6[2]), .in2(in_3[2]), .in3(in_4[2]), .out(out_8), .sel(in_2), .en(in_1));
  Multiplexer #(.select(2)) multiplexer_3 (
    .in0(in_5[1]), .in1(in_6[1]), .in2(in_3[1]), .in3(in_4[1]), .out(out_9), .sel(in_2), .en(in_1));
  Multiplexer #(.select(2)) multiplexer_4 (
    .in0(in_5[0]), .in1(in_6[0]), .in2(in_3[0]), .in3(in_4[0]), .out(out_10), .sel(in_2), .en(in_1));
endmodule

module BASIC_ALU (
  input  [3:0] A,
  input  [3:0] B,
  input  [2:0] in_3,
  output [3:0] out_4
);

  wire [3:0] adder_1_out, divider_1_out, multiplier_1_out, subtractor_1_out;

  Adder #(.width(4)) adder_1 (.a(A), .b(B), .out(adder_1_out));  // open: cin, cout
  Subtractor #(.width(4)) subtractor_1 (.a(A), .b(B), .out(subtractor_1_out));  // open: bin, bout
  Multiplier #(.width(4)) multiplier_1 (.a(A), .b(B), .out(multiplier_1_out));  // open: cin, cout
  Divider #(.width(4)) divider_1 (.a(A), .b(B), .out(divider_1_out));  // open: upper, rem
  Multiplexer #(.select(3), .width(4)) multiplexer_1 (
    .in0(adder_1_out), .in1(subtractor_1_out), .in2(multiplier_1_out), .in3(divider_1_out), .out(out_4),
    .sel(in_3));  // open: in4, in5, in6, in7, en

  // Notes on the sheet:
  //   ADDER
  //   SUBTRACTOR
  //   MULTIPLIER
  //   DIVIDER
  //   8:1 MULTIPLEXER
  //   MULTIPLEXER BITS
  //   OUTPUT
endmodule
